// Logisim project EXERCÍCIOS.circ as structural Verilog: 1 circuit, main circuit main
module main (
  input  in_1,
  input  in_2,
  input  in_3,
  input  in_4,
  input  in_5,
  input  [1:0] in_6,
  input  [1:0] in_7,
  input  in_8,
  input  in_9,
  input  [1:0] in_10,
  input  [1:0] in_11,
  input  in_12
);

  wire demultiplexer_1_out0, demultiplexer_1_out1, demultiplexer_1_out2, demultiplexer_1_out3,
       demultiplexer_2_out0, demultiplexer_2_out1, demultiplexer_2_out2, demultiplexer_2_out3,
       multiplexer_1_out, multiplexer_2_out;

  Multiplexer #(.select(2)) multiplexer_1 (
    .in0(in_4), .in1(in_2), .in2(in_3), .in3(in_1), .out(multiplexer_1_out), .sel(in_7), .en(in_8));
  Multiplexer #(.select(2)) multiplexer_2 (
    .in0(in_1), .in1(in_2), .in2(in_3), .in3(in_4), .out(multiplexer_2_out), .sel(in_11), .en(in_12));
  Demultiplexer #(.select(2)) demultiplexer_1 (
    .out0(demultiplexer_1_out0), .out1(demultiplexer_1_out1), .out2(demultiplexer_1_out2),
    .out3(demultiplexer_1_out3), .in(multiplexer_1_out), .sel(in_6), .en(in_5));
  Demultiplexer #(.select(2)) demultiplexer_2 (
    .out0(demultiplexer_2_out0), .out1(demultiplexer_2_out1), .out2(demultiplexer_2_out2),
    .out3(demultiplexer_2_out3), .in(multiplexer_2_out), .sel(in_10), .en(in_9));
  _7_Segment_Display #(.active("false")) u_7_segment_display_1 (
    .g(demultiplexer_1_out3), .f(demultiplexer_1_out2), .a(demultiplexer_1_out1), .b(demultiplexer_1_out0),
    .e(demultiplexer_2_out0), .d(demultiplexer_2_out1), .c(demultiplexer_2_out2), .dp(demultiplexer_2_out3));
endmodule
